// Logisim project bfcomp1.circ as structural Verilog: 10 circuits, main circuit final_circuit
module RAM_example (
);

  wire Clock, DecrAddr, IncrAddr, or_1_out, or_2_out, Reset;
  wire [7:0] counter_1_q, Data;

  Button button_1 (.out(DecrAddr));
  Button button_2 (.out(IncrAddr));
  or or_1 (or_1_out, DecrAddr, IncrAddr);
  Counter counter_1 (.load(DecrAddr), .count(or_1_out), .Q(counter_1_q), .clk(or_2_out));  // open: D, carry, clr
  or or_2 (or_2_out, DecrAddr, IncrAddr);
  Button button_3 (.out(Clock));
  RAM ram_1 (.addr(counter_1_q), .data(Data), .sel(1'b1), .clk(Clock), .ld(1'b0), .clr(Reset));
  Button button_4 (.out(Reset));
  // also tied to VCC on the sheet: {Data[0], Data[1], Data[2], Data[3], Data[4], Data[5], Data[6], Data[7]}

  // Notes on the sheet:
  //   When 1 data present on output. When 0 data gets read on clock
endmodule

// Sequential Memory
module sequential_memory_impl (
  input  [7:0] DIN,
  input  RESET,
  input  [2:0] CTLIn,
  input  [2:0] ACCtl,
  output [7:0] do1,
  output [7:0] do2,
  output [7:0] do3,
  output [7:0] do4,
  output [7:0] do5,
  output [7:0] do6,
  output [7:0] do7,
  output [7:0] do8,
  output [6:0] ASCII,
  output [7:0] DOUT,
  output [7:0] ADDR
);

  wire [2:0] C1, C2, C3, C4, C5, C6, C7, C8, counter_1_q;

  Demultiplexer #(.select(3), .width(3), .disabled(0), .enable("false")) demultiplexer_1 (
    .out0(C1), .out1(C2), .out2(C3), .out3(C4), .out4(C5), .out5(C6), .out6(C7), .out7(C8), .in(CTLIn),
    .sel(counter_1_q));
  ctr_impl ctr_impl_1 (.DIn(DIN), .Ctl(C1), .RST(RESET), .Dout(do1));
  ctr_impl ctr_impl_2 (.DIn(DIN), .Ctl(C5), .RST(RESET), .Dout(do5));
  Counter #(.width(3), .max('h7)) counter_1 (
    .load(ACCtl[0]), .count(ACCtl[1]), .Q(counter_1_q), .clk(ACCtl[2]), .clr(RESET));  // open: D, carry
  ctr_impl ctr_impl_3 (.DIn(DIN), .Ctl(C2), .RST(RESET), .Dout(do2));
  ctr_impl ctr_impl_4 (.DIn(DIN), .Ctl(C6), .RST(RESET), .Dout(do6));
  ctr_impl ctr_impl_5 (.DIn(DIN), .Ctl(C3), .RST(RESET), .Dout(do3));
  ctr_impl ctr_impl_6 (.DIn(DIN), .Ctl(C7), .RST(RESET), .Dout(do7));
  Multiplexer #(.select(3), .width(8), .disabled(0), .enable("false")) multiplexer_1 (
    .in0(do1), .in1(do2), .in2(do3), .in3(do4), .in4(do5), .in5(do6), .in6(do7), .in7(do8),
    .out({DOUT[7], ASCII}), .sel(counter_1_q));
  ctr_impl ctr_impl_7 (.DIn(DIN), .Ctl(C4), .RST(RESET), .Dout(do4));
  ctr_impl ctr_impl_8 (.DIn(DIN), .Ctl(C8), .RST(RESET), .Dout(do8));
  addr_decoder_impl Address_Encoder (.IN(counter_1_q), .OUT(ADDR));

  assign DOUT[6:0] = ASCII;

  // Other names for the same wires on the sheet: C1o[7:0] = do1; C2o[7:0] = do2; C3o[7:0] = do3; C4o[7:0] = do4;
  //   C5o[7:0] = do5; C6o[7:0] = do6; C7o[7:0] = do7; C8o[7:0] = do8
endmodule

// Ctr
module ctr_impl (
  input  [7:0] DIn,
  input  [2:0] Ctl,
  input  RST,
  output [7:0] Dout
);

  Counter counter_1 (.load(Ctl[0]), .D(DIn), .count(Ctl[1]), .Q(Dout), .clk(Ctl[2]), .clr(RST));  // open: carry
endmodule

module sequential_memory_example (
);

  wire RESET;
  wire [2:0] ADDRCTL_3, CTL_3;
  wire [6:0] DOUT_7;
  wire [7:0] CADDR_8, DIN_8, sequential_memory_impl_1_do1, sequential_memory_impl_1_do2,
       sequential_memory_impl_1_do3, sequential_memory_impl_1_do4, sequential_memory_impl_1_do5,
       sequential_memory_impl_1_do6, sequential_memory_impl_1_do7, sequential_memory_impl_1_do8;

  DotMatrix #(.matrixcols(8), .matrixrows(8), .dotshape("circle")) dotmatrix_1 (
    .col0(sequential_memory_impl_1_do1), .col1(sequential_memory_impl_1_do2),
    .col2(sequential_memory_impl_1_do3), .col3(sequential_memory_impl_1_do4),
    .col4(sequential_memory_impl_1_do5), .col5(sequential_memory_impl_1_do6),
    .col6(sequential_memory_impl_1_do7), .col7(sequential_memory_impl_1_do8));
  sequential_memory_impl sequential_memory_impl_1 (
    .DIN(DIN_8), .ASCII(DOUT_7), .CTLIn(CTL_3), .RESET(RESET), .do1(sequential_memory_impl_1_do1),
    .do2(sequential_memory_impl_1_do2), .do3(sequential_memory_impl_1_do3),
    .do4(sequential_memory_impl_1_do4), .do5(sequential_memory_impl_1_do5),
    .do6(sequential_memory_impl_1_do6), .do7(sequential_memory_impl_1_do7),
    .do8(sequential_memory_impl_1_do8), .ACCtl(ADDRCTL_3), .ADDR(CADDR_8));  // open: DOUT

  // Notes on the sheet:
  //   LED array
endmodule

module four_commands (
);

  wire clock_1_out, not_1_out;
  wire [1:0] rom_1_data;
  wire [2:0] demultiplexer_1_out0, demultiplexer_1_out1, PC;
  wire [3:0] rom_2_data;
  wire [6:2] rom_1_data_2;
  wire [7:0] counter_2_q, PC_q, sequential_memory_impl_1_addr, sequential_memory_impl_1_do1,
       sequential_memory_impl_1_do2, sequential_memory_impl_1_do3, sequential_memory_impl_1_do4,
       sequential_memory_impl_1_do5, sequential_memory_impl_1_do6, sequential_memory_impl_1_do7,
       sequential_memory_impl_1_do8;

  Clock clock_1 (.out(clock_1_out));
  Counter #(.width(2), .max('h3)) counter_1 (
    .load(1'b1), .D(rom_1_data), .count(1'b0), .Q(rom_2_data[1:0]), .clk(clock_1_out));  // open: carry, clr
  Counter counter_2 (.load(1'b1), .D(PC_q), .count(1'b0), .Q(counter_2_q), .clk(not_1_out));  // open: carry, clr
  Counter u_PC (.load(PC[0]), .count(PC[1]), .Q(PC_q), .clk(PC[2]));  // open: D, carry, clr
  not not_1 (not_1_out, PC[2]);
  ROM #(.addrWidth(4), .dataWidth(7)) rom_1 (.addr(rom_2_data), .data({rom_1_data_2, rom_1_data}));  // open: sel
  ROM #(.dataWidth(2)) rom_2 (.addr(counter_2_q), .data(rom_2_data[3:2]));  // open: sel
  Demultiplexer #(.select(2), .width(3), .disabled(0), .enable("false")) demultiplexer_1 (
    .out0(demultiplexer_1_out0), .out1(demultiplexer_1_out1), .out3(PC),
    .in({rom_1_data_2[4], rom_1_data_2[5], rom_1_data_2[6]}), .sel(rom_1_data_2[3:2]));  // open: out2
  DotMatrix #(.inputtype("row"), .matrixcols(8), .matrixrows(1), .dotshape("circle")) dotmatrix_1 (.row0(sequential_memory_impl_1_addr));
  DotMatrix #(.matrixcols(8), .matrixrows(8), .dotshape("circle")) dotmatrix_2 (
    .col0(sequential_memory_impl_1_do1), .col1(sequential_memory_impl_1_do2),
    .col2(sequential_memory_impl_1_do3), .col3(sequential_memory_impl_1_do4),
    .col4(sequential_memory_impl_1_do5), .col5(sequential_memory_impl_1_do6),
    .col6(sequential_memory_impl_1_do7), .col7(sequential_memory_impl_1_do8));
  sequential_memory_impl sequential_memory_impl_1 (
    .CTLIn(demultiplexer_1_out0), .do1(sequential_memory_impl_1_do1), .do2(sequential_memory_impl_1_do2),
    .do3(sequential_memory_impl_1_do3), .do4(sequential_memory_impl_1_do4),
    .do5(sequential_memory_impl_1_do5), .do6(sequential_memory_impl_1_do6),
    .do7(sequential_memory_impl_1_do7), .do8(sequential_memory_impl_1_do8), .ACCtl(demultiplexer_1_out1),
    .ADDR(sequential_memory_impl_1_addr));  // open: DIN, ASCII, RESET, DOUT

  // Notes on the sheet:
  //   PCL
  //   Control ROM
  //   Program ROM
  //   contents of rom_1 (hex, n*v repeats v):
  //   21 32 2f 3c 61 72 2f 3c 25 36 2f 3c 65 76 2f 3c
  //   contents of rom_2 (hex, n*v repeats v):
  //   0 2 0 0 2 0 0 0 1 1 1 3 1 1 3 1 0 2 0 0 2 0 0 0 1 1 1 3 1 1 3 1 0 2 0 0 2 0 0 0 1 1 1 3 1 1 3 1 0 2
  //   0 0 2 0 0 0 1 1 1 3 1 1 3 1
endmodule

module addr_decoder_impl (
  input  [2:0] IN,
  output [7:0] OUT
);

  Decoder #(.select(3), .disabled(0), .enable("false")) decoder_1 (
    .out0(OUT[7]), .out1(OUT[6]), .out2(OUT[5]), .out3(OUT[4]), .out4(OUT[3]), .out5(OUT[2]), .out6(OUT[1]),
    .out7(OUT[0]), .sel(IN));
endmodule

module six_commands (
);

  wire clock_1_out, ct, hl, HLT, j_k_ff_1_qn, j_k_ff_2_qn, not_2_out;
  wire [2:0] counter_1_q, counter_2_q, demultiplexer_1_out0, demultiplexer_1_out1, PC, rom_1_data, rom_2_data;
  wire [6:0] sequential_memory_impl_1_ascii;
  wire [7:0] progcounter_impl_1_out_2, sequential_memory_impl_1_addr, sequential_memory_impl_1_do1,
       sequential_memory_impl_1_do2, sequential_memory_impl_1_do3, sequential_memory_impl_1_do4,
       sequential_memory_impl_1_do5, sequential_memory_impl_1_do6, sequential_memory_impl_1_do7,
       sequential_memory_impl_1_do8;
  wire [8:3] rom_2_data_2;

  J_K_Flip_Flop j_k_ff_1 (.Qn(j_k_ff_1_qn), .preset(j_k_ff_2_qn), .reset(ct));  // open: J, clk, K, Q, en
  J_K_Flip_Flop j_k_ff_2 (.J(HLT), .clk(clock_1_out), .K(j_k_ff_1_qn), .Qn(j_k_ff_2_qn));  // open: Q, preset, en, reset
  Clock clock_1 (.out(clock_1_out));
  not not_1 (hl, j_k_ff_2_qn);
  progcounter_impl progcounter_impl_1 (.in_1(PC), .out_2(progcounter_impl_1_out_2));
  Counter #(.width(3), .max('h7)) counter_1 (
    .load(j_k_ff_2_qn), .D(rom_2_data), .count(1'b0), .Q(counter_1_q), .clk(clock_1_out));  // open: carry, clr
  Counter #(.width(3), .max('h7)) counter_2 (
    .load(1'b1), .D(counter_1_q), .count(1'b0), .Q(counter_2_q), .clk(not_2_out));  // open: carry, clr
  not not_2 (not_2_out, clock_1_out);
  DotMatrix #(.inputtype("row"), .matrixcols(8), .matrixrows(1), .dotshape("circle")) dotmatrix_1 (.row0(sequential_memory_impl_1_addr));
  DotMatrix #(.matrixcols(8), .matrixrows(8), .dotshape("circle")) dotmatrix_2 (
    .col0(sequential_memory_impl_1_do1), .col1(sequential_memory_impl_1_do2),
    .col2(sequential_memory_impl_1_do3), .col3(sequential_memory_impl_1_do4),
    .col4(sequential_memory_impl_1_do5), .col5(sequential_memory_impl_1_do6),
    .col6(sequential_memory_impl_1_do7), .col7(sequential_memory_impl_1_do8));
  ROM #(.dataWidth(3)) rom_1 (.addr(progcounter_impl_1_out_2), .data(rom_1_data));  // open: sel
  sequential_memory_impl sequential_memory_impl_1 (
    .DIN(8'h64), .ASCII(sequential_memory_impl_1_ascii), .CTLIn(demultiplexer_1_out0),
    .do1(sequential_memory_impl_1_do1), .do2(sequential_memory_impl_1_do2),
    .do3(sequential_memory_impl_1_do3), .do4(sequential_memory_impl_1_do4),
    .do5(sequential_memory_impl_1_do5), .do6(sequential_memory_impl_1_do6),
    .do7(sequential_memory_impl_1_do7), .do8(sequential_memory_impl_1_do8), .ACCtl(demultiplexer_1_out1),
    .ADDR(sequential_memory_impl_1_addr));  // open: RESET, DOUT
  TTY #(.rows(4), .cols(20)) tty_1 (.data(sequential_memory_impl_1_ascii), .clk(rom_2_data_2[8]));  // open: we, clr
  Button CONTINUE (.out(ct));
  Demultiplexer #(.select(2), .width(3), .disabled(0), .enable("false")) demultiplexer_1 (
    .out0(demultiplexer_1_out0), .out1(demultiplexer_1_out1), .out3(PC),
    .in({rom_2_data_2[5], rom_2_data_2[6], rom_2_data_2[7]}), .sel(rom_2_data_2[4:3]));  // open: out2
  ROM #(.addrWidth(6), .dataWidth(10)) rom_2 (
    .addr({rom_1_data, counter_2_q}), .data({HLT, rom_2_data_2, rom_2_data}));  // open: sel
  LED HALT (.in(hl));

  // Notes on the sheet:
  //   "User Input" value
  //   Program ROM
  //   contents of rom_1 (hex, n*v repeats v):
  //   5 2 5 2 5 2 5 2 5 2 5 2 5 2 5 0 0 3 0 3 0 3 1 1 3 3 1 1 1 3 0 3 4 2 4 2 4 2 4 2 4 2 4 2 4 2 4 5
  //   Control ROM
  //   contents of rom_2 (hex, n*v repeats v):
  //   41 62 5b 78 4*0 c1 e2 5b 78 4*0 49 6a 5b 78 4*0 c9 ea 5b 78 4*0 11 112 5b 78 4*0 211 82 a3 5c 78
endmodule

// PC
module progcounter_impl (
  input  [2:0] in_1,
  output [7:0] out_2
);

  wire not_1_out;
  wire [7:0] counter_1_q;

  Counter counter_1 (.load(in_1[0]), .count(in_1[1]), .Q(counter_1_q), .clk(in_1[2]));  // open: D, carry, clr
  Counter counter_2 (.load(1'b1), .D(counter_1_q), .count(1'b0), .Q(out_2), .clk(not_1_out));  // open: carry, clr
  not not_1 (not_1_out, in_1[2]);
endmodule

module display_demo (
);

  wire clock_1_out;
  wire [6:0] rom_1_data;
  wire [7:0] counter_1_q;

  Counter counter_1 (.Q(counter_1_q), .clk(clock_1_out));  // open: load, D, count, carry, clr
  Clock clock_1 (.out(clock_1_out));
  ROM #(.dataWidth(7)) rom_1 (.addr(counter_1_q), .data(rom_1_data));  // open: sel
  TTY tty_1 (.data(rom_1_data), .clk(clock_1_out));  // open: we, clr

  // Notes on the sheet:
  //   contents of rom_1 (hex, n*v repeats v):
  //   4c 6f 72 65 6d 20 69 70 73 75 6d 20 64 6f 6c 6f 72 20 73 69 74 20 61 6d 65 74 2c 20 63 6f 6e 73 65
  //   63 74 65 74 75 72 20 61 64 69 70 69 73 63 69 6e 67 20 65 6c 69 74 2c 20 73 65 64 20 64 6f 20 65 69
  //   75 73 6d 6f 64 20 74 65 6d 70 6f 72 20 69 6e 63 69 64 69 64 75 6e 74 20 75 74 20 6c 61 62 6f 72 65
  //   20 65 74 20 64 6f 6c 6f 72 65 20 6d 61 67 6e 61 20 61 6c 69 71 75 61 2e 20 55 74 20 65 6e 69 6d 20
  //   61 64 20 6d 69 6e 69 6d 20 76 65 6e 69 61 6d 2c 20 71 75 69 73 20 6e 6f 73 74 72 75 64 20 65 78 65
  //   72 63 69 74 61 74 69 6f 6e 20 75 6c 6c 61 6d 63 6f 20 6c 61 62 6f 72 69 73 20 6e 69 73 69 20 75 74
  //   20 61 6c 69 71 75 69 70 20 65 78 20 65 61 20 63 6f 6d 6d 6f 64 6f 20 63 6f 6e 73 65 71 75 61 74 2e
  //   20 44 75 69 73 20 61 75 74 65 20 69 72 75 72 65 20 64 6f 6c 6f 72 20 69 6e
endmodule

module final_circuit (
);

  wire BM, CLK, ct, hl, HLT, j_k_ff_1_qn, j_k_ff_2_qn, MDir, not_2_out, not_3_out, Oclk, TMot;
  wire [2:0] ACtl, BCtr, counter_3_q, counter_4_q, CTLIn, PC, rom_1_data, rom_2_data;
  wire [3:0] FLags, FLatch_q;
  wire [6:0] sequential_memory_impl_1_ascii;
  wire [7:0] BCtr_q, counter_1_q, counter_2_q, DATA, sequential_memory_impl_1_addr,
       sequential_memory_impl_1_do1, sequential_memory_impl_1_do2, sequential_memory_impl_1_do3,
       sequential_memory_impl_1_do4, sequential_memory_impl_1_do5, sequential_memory_impl_1_do6,
       sequential_memory_impl_1_do7, sequential_memory_impl_1_do8;
  wire [8:3] rom_2_data_2;

  J_K_Flip_Flop j_k_ff_1 (.Qn(j_k_ff_1_qn), .preset(j_k_ff_2_qn), .reset(ct));  // open: J, clk, K, Q, en
  T_Flip_Flop MF (.clk(CLK), .T(TMot), .Q(FLags[2]));  // open: Qn, preset, reset, en
  not not_1 (hl, j_k_ff_2_qn);
  J_K_Flip_Flop j_k_ff_2 (.J(HLT), .clk(CLK), .K(j_k_ff_1_qn), .Qn(j_k_ff_2_qn));  // open: Q, preset, en, reset
  Counter counter_1 (.load(PC[0]), .count(PC[1]), .Q(counter_1_q), .clk(PC[2]));  // open: D, carry, clr
  Counter counter_2 (.load(1'b1), .D(counter_1_q), .count(1'b0), .Q(counter_2_q), .clk(not_2_out));  // open: carry, clr
  not not_2 (not_2_out, PC[2]);
  T_Flip_Flop MD (.clk(CLK), .T(MDir), .Q(FLags[0]));  // open: Qn, preset, reset, en
  Counter #(.width(3), .max('h7)) counter_3 (
    .load(j_k_ff_2_qn), .D(rom_2_data), .count(1'b0), .Q(counter_3_q), .clk(CLK));  // open: carry, clr
  not not_3 (not_3_out, CLK);
  Counter #(.width(4), .max('hf)) FLatch (
    .load(1'b1), .D({FLags[3:2], BM, FLags[0]}), .count(1'b0), .Q(FLatch_q), .clk(not_2_out));  // open: carry, clr
  ROM #(.dataWidth(3)) rom_1 (.addr(counter_2_q), .data(rom_1_data));  // open: sel
  Counter u_BCtr (.load(BCtr[0]), .count(BCtr[1]), .Q(BCtr_q), .clk(BCtr[2]));  // open: D, carry, clr
  Counter #(.width(3), .max('h7)) counter_4 (
    .load(1'b1), .D(counter_3_q), .count(1'b0), .Q(counter_4_q), .clk(not_3_out));  // open: carry, clr
  DotMatrix #(.inputtype("row"), .matrixcols(8), .matrixrows(1), .dotshape("circle")) dotmatrix_1 (.row0(sequential_memory_impl_1_addr));
  DotMatrix #(.matrixcols(8), .matrixrows(8), .dotshape("circle")) dotmatrix_2 (
    .col0(sequential_memory_impl_1_do1), .col1(sequential_memory_impl_1_do2),
    .col2(sequential_memory_impl_1_do3), .col3(sequential_memory_impl_1_do4),
    .col4(sequential_memory_impl_1_do5), .col5(sequential_memory_impl_1_do6),
    .col6(sequential_memory_impl_1_do7), .col7(sequential_memory_impl_1_do8));
  sequential_memory_impl sequential_memory_impl_1 (
    .ASCII(sequential_memory_impl_1_ascii), .CTLIn(CTLIn), .do1(sequential_memory_impl_1_do1),
    .do2(sequential_memory_impl_1_do2), .do3(sequential_memory_impl_1_do3),
    .do4(sequential_memory_impl_1_do4), .do5(sequential_memory_impl_1_do5),
    .do6(sequential_memory_impl_1_do6), .do7(sequential_memory_impl_1_do7),
    .do8(sequential_memory_impl_1_do8), .ACCtl(ACtl), .ADDR(sequential_memory_impl_1_addr), .DOUT(DATA));  // open: DIN, RESET
  nor nor_1 (BM, BCtr_q[0], BCtr_q[1], BCtr_q[2], BCtr_q[3], BCtr_q[5], BCtr_q[6], BCtr_q[7], BCtr_q[4]);
  ROM #(.addrWidth(10), .dataWidth(13)) rom_2 (
    .addr({rom_1_data, FLatch_q, counter_4_q}), .data({TMot, MDir, HLT, Oclk, rom_2_data_2, rom_2_data}));  // open: sel
  TTY #(.rows(4), .cols(20)) tty_1 (.data(sequential_memory_impl_1_ascii), .clk(Oclk));  // open: we, clr
  Button CONTINUE (.out(ct));
  nor ZF (FLags[3], DATA[0], DATA[1], DATA[2], DATA[3], DATA[5], DATA[6], DATA[7], DATA[4]);
  Demultiplexer #(.select(3), .width(3), .disabled(0), .enable("false")) demultiplexer_1 (
    .out0(CTLIn), .out1(ACtl), .out3(PC), .out4(BCtr),
    .in({rom_2_data_2[6], rom_2_data_2[7], rom_2_data_2[8]}), .sel(rom_2_data_2[5:3]));  // open: out2, out5, out6, out7
  Clock clock_1 (.out(CLK));
  LED HALT (.in(hl));

  // Other names for the same wires on the sheet: MD = FLags[0]; FLags[1] = BM; MF = FLags[2]

  // Notes on the sheet:
  //   contents of rom_1 (hex, n*v repeats v):
  //   8*0 6 2 4*0 6 2 0 0 2 0 0 0 2 0 0 0 2 0 4*3 1 7 2 0 2 0 2 1 2 2 0 6 3 7 3 1 7 2 2 4 2 1 1 1 4 7*0 4
  //   4 0 0 0 4 2 2 4 3 1 4 3 4 0 0 0 4 6*1 4 8*1 4 2 2 0 4 2 0 0 4 5
  //   ----------------------------------------------------------------------------------------------------------------------------------------
  //   Control ROM
  //   contents of rom_2 (hex, n*v repeats v):
  //   81 c2 9b d8 4*0 81 c2 9b d8 4*0 81 c2 9b d8 4*0 81 c2 9b d8 4*0 99 d8 6*0 199 1d8 6*0 99 d8 6*0 199
  //   1d8 6*0 81 c2 9b d8 4*0 81 c2 9b d8 4*0 81 c2 9b d8 4*0 81 c2 9b d8 4*0 99 d8 6*0 199 1d8 6*0 99 d8
  //   6*0 199 1d8 6*0 181 1c2 9b d8 4*0 181 1c2 9b d8 4*0 181 1c2 9b d8 4*0 181 1c2 9b d8 4*0 99 d8 6*0
  //   199 1d8 6*0 99 d8 6*0 199 1d8 6*0 181 1c2 9b d8 4*0 181 1c2 9b d8 4*0 181 1c2 9b d8 4*0 181 1c2 9b
  //   d8 4*0 99 d8 6*0 199 1d8 6*0 99 d8 6*0 199 1d8 6*0 89 ca 9b d8 4*0 89 ca 9b d8 4*0 89 ca 9b d8 4*0
  //   89 ca 9b d8 4*0 99 d8 6*0 199 1d8 6*0 99 d8 6*0 199 1d8 6*0 89 ca 9b d8 4*0 89 ca 9b d8 4*0 89 ca 9b
  //   d8 4*0 89 ca 9b d8 4*0 99 d8 6*0 199 1d8 6*0 99 d8 6*0 199 1d8 6*0 189 1ca 9b d8 4*0 189 1ca 9b d8
  //   4*0 189 1ca 9b d8 4*0 189 1ca 9b d8 4*0 99 d8 6*0 199 1d8 6*0 99 d8 6*0 199 1d8 6*0 189 1ca 9b d8
  //   4*0 189 1ca 9b d8 4*0 189 1ca 9b d8 4*0 189 1ca 9b d8 4*0 99 d8 6*0 199 1d8 6*0 99 d8 6*0 199 1d8
  //   6*0 11 212 9b d8 4*0 11 212 9b d8 4*0 11 212 9b d8 4*0 11 212 9b d8 4*0 99 d8 6*0 199 1d8 6*0 99 d8
  //   6*0 199 1d8 6*0 11 212 9b d8 4*0 11 212 9b d8 4*0 11 212 9b d8 4*0 11 212 9b d8 4*0 99 d8 6*0 199
  //   1d8 6*0 99 d8 6*0 199 1d8 6*0 411 102 143 9c d8 0 0 0 411 102 143 9c d8 0 0 0 411 102 143 9c d8 0 0
  //   0 411 102 143 9c d8 0 0 0 99 d8 6*0 199 1d8 6*0 99 d8 6*0 199 1d8 6*0 411 102 143 9c d8 0 0 0 411
  //   102 143 9c d8 0 0 0 411 102 143 9c d8 0 0 0 411 102 143 9c d8 0 0 0 99 d8 6*0 199 1d8 6*0 99 d8 6*0
  //   199 1d8 6*0 99 d8 6*0 99 d8 6*0 99 d8 6*0 99 d8 6*0 a1 e2 9b d8 4*0 1a1 1e2 19b 1d8 4*0 a1 e2 9b d8
  //   4*0 1811 9a d8 5*0 1099 d8 6*0 1099 d8 6*0 1099 d8 6*0 1099 d8 6*0 a1 e2 9b d8 4*0 1a1 1e2 19b 1d8
  //   4*0 a1 e2 9b d8 4*0 1811 9a d8 5*0 1999 1d8 6*0 1999 1d8 6*0 1999 1d8 6*0 1999 1d8 6*0 1a1 1e2 9b d8
  //   4*0 a1 e2 19b 1d8 4*0 1011 9a d8 5*0 a1 e2 19b 1d8 4*0 99 d8 6*0 99 d8 6*0 99 d8 6*0 99 d8 6*0 1a1
  //   1e2 9b d8 4*0 a1 e2 19b 1d8 4*0 1011 9a d8 5*0 a1 e2 19b 1d8
endmodule
