// Logisim project complex_plexer.circ as structural Verilog: 1 circuit, main circuit main
module main (
);

  wire clock_1_out, demultiplexer_1_out0, demultiplexer_1_out1, demultiplexer_1_out2;
  wire [7:0] counter_1_q, counter_2_q, counter_3_q, multiplexer_1_out;

  Clock clock_1 (.out(clock_1_out));
  Demultiplexer #(.select(2)) demultiplexer_1 (
    .out0(demultiplexer_1_out0), .out1(demultiplexer_1_out1), .out2(demultiplexer_1_out2), .in(clock_1_out),
    .sel(2'b00), .en(1'b1));  // open: out3
  Counter counter_1 (
    .load(1'b1), .D(multiplexer_1_out), .count(1'b0), .Q(counter_1_q), .clk(demultiplexer_1_out0));  // open: carry, clr
  Counter counter_2 (
    .load(1'b1), .D(multiplexer_1_out), .count(1'b0), .Q(counter_2_q), .clk(demultiplexer_1_out1));  // open: carry, clr
  Counter counter_3 (
    .load(1'b1), .D(multiplexer_1_out), .count(1'b0), .Q(counter_3_q), .clk(demultiplexer_1_out2));  // open: carry, clr
  Multiplexer #(.select(2), .width(8)) multiplexer_1 (
    .in0(8'hea), .in1(counter_1_q), .in2(counter_2_q), .in3(counter_3_q), .out(multiplexer_1_out),
    .sel(2'b10), .en(1'b1));

  // Notes on the sheet:
  //   Destination
  //   Source
  //   Reg A
  //   Reg B
  //   Reg C
endmodule
