// Logisim project lad_lai.circ as structural Verilog: 1 circuit, main circuit main
module main (
);

  wire clock_1_out;
  wire [1:0] Address_2_q, Address_q;
  wire [2:0] multiplexer_1_out, multiplexer_2_out, multiplexer_3_out;

  Clock clock_1 (.out(clock_1_out));
  Multiplexer #(.select(2), .width(3)) multiplexer_1 (
    .in0(3'b100), .in1(3'b101), .in2(3'b010), .in3(3'b011), .out(multiplexer_1_out), .sel(Address_q),
    .en(1'b1));
  Counter #(.width(2), .max('h3)) Address (
    .load(1'b0), .count(1'b1), .Q(Address_q), .clk(clock_1_out));  // open: D, carry, clr
  Multiplexer #(.select(2), .width(3)) multiplexer_2 (
    .in0(3'b100), .in1(3'b101), .in2(3'b110), .in3(3'b111), .out(multiplexer_2_out), .sel(Address_2_q),
    .en(1'b1));
  Counter #(.width(2), .max('h3)) Address_2 (
    .load(1'b0), .count(1'b1), .Q(Address_2_q), .clk(clock_1_out));  // open: D, carry, clr
  Multiplexer #(.width(3)) multiplexer_3 (
    .in0(multiplexer_1_out), .in1(multiplexer_2_out), .out(multiplexer_3_out), .sel(1'b0), .en(1'b1));
  Counter counter_1 (
    .load(multiplexer_3_out[2]), .D(8'hea), .count(multiplexer_3_out[1]), .clk(multiplexer_3_out[0]));  // open: Q, carry, clr

  // Notes on the sheet:
  //   L  C  Clk
  //   LAI
  //   L  C  Clk
  //   LAD
  //   Inst Sel
  //   Inst Code:
  //   0 - LAI
  //   1 - LAD
endmodule
