// Logisim project lailadrom.circ as structural Verilog: 1 circuit, main circuit main
module main (
);

  wire clock_1_out, not_1_out;
  wire [1:0] rom_1_data;
  wire [2:0] counter_1_q, counter_2_q;
  wire [5:2] rom_1_data_2;

  Counter #(.width(2), .max('h3)) counter_1 (
    .D(rom_1_data), .Q(counter_1_q[1:0]), .clk(clock_1_out));  // open: load, count, carry, clr
  Clock clock_1 (.out(clock_1_out));
  Counter #(.width(3), .max('h7)) counter_2 (
    .load(1'b0), .count(1'b1), .Q(counter_2_q), .clk(not_1_out));  // open: D, carry, clr
  // Probe on {rom_1_data_2, rom_1_data}
  ROM #(.addrWidth(3), .dataWidth(6)) rom_1 (.addr(counter_1_q), .data({rom_1_data_2, rom_1_data}));  // open: sel
  not not_1 (not_1_out, rom_1_data_2[2]);
  // Probe on counter_1_q[2]
  ROM #(.addrWidth(3), .dataWidth(1)) rom_2 (.addr(counter_2_q), .data(counter_1_q[2]));  // open: sel
  Counter counter_3 (
    .load(rom_1_data_2[5]), .D(8'hea), .count(rom_1_data_2[4]), .clk(rom_1_data_2[3]));  // open: Q, carry, clr

  // Notes on the sheet:
  //   Next Step
  //   PC
  //   Control ROM
  //   Program
  //   contents of rom_1 (hex, n*v repeats v):
  //   21 2a 13 1c 21 2a 33 3c
  //   contents of rom_2 (hex, n*v repeats v):
  //   1 0 0 1 0 1 1 1
endmodule
