// Logisim project rom_cu_general.circ as structural Verilog: 1 circuit, main circuit main
module main (
);

  wire clock_1_out;
  wire [2:0] register_1_q;
  wire [7:0] rom_1_data;

  Register #(.width(3)) register_1 (.D(rom_1_data[7:5]), .Q(register_1_q), .clk(clock_1_out));  // open: en, clr
  Clock clock_1 (.out(clock_1_out));
  ROM rom_1 (.addr({register_1_q, 5'b11110}), .data(rom_1_data));  // open: sel
  // Probe on rom_1_data[4:0]
  // Probe on rom_1_data[7:5]

  // Notes on the sheet:
  //   Instruction
  //   Next Step Latch
  //   contents of rom_1 (hex, n*v repeats v):
  //   16*0 cc be ef 4 12 4 5 60 ea 13 ea a 40 ae 1d 1 49*0 df 0 5 6 ea
  //   Control Table Entry
  //   Next Step
endmodule
