// Logisim project simple_plexer.circ as structural Verilog: 1 circuit, main circuit main
module main (
);

  wire clock_1_out;
  wire [1:0] Address_q;
  wire [2:0] multiplexer_1_out;

  Clock clock_1 (.out(clock_1_out));
  Multiplexer #(.select(2), .width(3)) multiplexer_1 (
    .in0(3'b100), .in1(3'b101), .in2(3'b010), .in3(3'b011), .out(multiplexer_1_out), .sel(Address_q),
    .en(1'b1));
  Counter #(.width(2), .max('h3)) Address (
    .load(1'b0), .count(1'b1), .Q(Address_q), .clk(clock_1_out));  // open: D, carry, clr
  Counter counter_1 (
    .load(multiplexer_1_out[2]), .D(8'hea), .count(multiplexer_1_out[1]), .clk(multiplexer_1_out[0]));  // open: Q, carry, clr

  // Notes on the sheet:
  //   Load   Count  Clock
  //   -----------------------------
endmodule
